# Fritzing sketch c4 (saved by Fritzing 0.9.3b)
breadboards: 1

parts:
  Raspberry_Pi_1 = Raspberry Pi 3 [part_number=RPI-3-V1.2]
  R7 = Photocell (LDR) [package=THT]
  C1 = Electrolytic Capacitor [capacitance=1µF package="100 mil [THT, electrolytic]"]

nets:
  N1: Raspberry_Pi_1.3v3, R7.pin_0
  N2: Raspberry_Pi_1.GPIO4, R7.pin_1, C1.+
  N3: Raspberry_Pi_1.GND, C1.-

notes:
  Circuito 4
